// Logisim project better_y86_processor.circ as structural Verilog
module PC_Logic (
);

  Register register_1 ();  // open: D, en, Q, clk, clr
  Adder adder_1 ();  // open: a, b, out, cin, cout
  Multiplexer #(.enable("false")) multiplexer_1 ();  // open: in0, in1, out, sel
endmodule

module ALU (
);

  // Odd_Parity odd_parity_1 is placed but not wired
endmodule
